// Logisim project Discrete_component_CPU_ROM.circ as structural Verilog: 1 circuit, main circuit main
module main (
  input  a,
  input  b,
  input  c,
  input  d,
  input  e,
  input  f,
  input  g,
  input  h,
  input  x2,
  input  x3,
  input  x4,
  output x,
  output y,
  output z,
  output u,
  output v,
  output w,
  output s,
  output t
);

  wire and_1_out, and_2_out, and_3_out, and_4_out, and_5_out, and_6_out, and_7_out, and_8_out, and_9_out,
       and_10_out, and_11_out, and_12_out, and_13_out, and_14_out, and_15_out, and_16_out, and_17_out,
       and_18_out, and_19_out, and_20_out, and_21_out, and_22_out, and_23_out, and_24_out, and_25_out,
       and_26_out, and_27_out, and_28_out, and_29_out, and_30_out, and_31_out, and_32_out, and_33_out,
       and_34_out, and_35_out, and_36_out, and_37_out, and_38_out, and_39_out, and_41_out, and_42_out,
       and_43_out, and_44_out, and_45_out, and_46_out, and_47_out, and_48_out, and_49_out, and_50_out,
       and_51_out, and_52_out, and_53_out, and_54_out, and_55_out, and_56_out, and_58_out, and_59_out,
       and_60_out, and_61_out, and_62_out, and_63_out, and_64_out, and_65_out, and_66_out, and_67_out,
       and_68_out, and_69_out, and_70_out, and_71_out, and_72_out, and_73_out, and_74_out, and_75_out,
       and_76_out, and_77_out, and_78_out, and_79_out, and_80_out, and_81_out, and_83_out, and_84_out,
       and_85_out, and_86_out, and_87_out, and_88_out, and_89_out, and_90_out, and_91_out, and_92_out,
       and_93_out, and_94_out, and_95_out, and_96_out, and_97_out, and_98_out, and_99_out, and_100_out,
       and_101_out, and_102_out, and_103_out, and_104_out, and_105_out, and_106_out, and_107_out,
       and_108_out, and_109_out, and_110_out, and_111_out, and_112_out, and_113_out, and_114_out,
       and_115_out, and_116_out, and_117_out, and_118_out, and_119_out, and_120_out, and_121_out,
       and_122_out, and_123_out, and_124_out, and_125_out, and_126_out, and_128_out, and_129_out,
       and_130_out, and_131_out, and_132_out, and_133_out, and_134_out, and_135_out, and_136_out,
       and_137_out, and_138_out, and_139_out, and_140_out, and_141_out, and_142_out, and_143_out,
       and_144_out, and_145_out, not_1_out, not_2_out, not_3_out, not_4_out, not_5_out, not_6_out, not_7_out,
       not_8_out, not_9_out, not_10_out, not_11_out, not_12_out, not_13_out, not_14_out, not_15_out,
       not_16_out, not_17_out, not_18_out, not_19_out, not_20_out, not_21_out, not_22_out, not_23_out,
       not_24_out, not_25_out, not_26_out, not_27_out, not_28_out, not_29_out, not_30_out, not_31_out,
       not_32_out, not_33_out, not_34_out, not_35_out, not_36_out, not_37_out, not_38_out, not_39_out,
       not_40_out, not_41_out, not_42_out, not_43_out, not_44_out, not_45_out, not_46_out, not_47_out,
       not_48_out, not_49_out, not_50_out, not_51_out, not_52_out, not_53_out, not_54_out, not_55_out,
       not_56_out, not_57_out, not_58_out, not_59_out, not_60_out, not_61_out, not_62_out, not_63_out,
       not_64_out, not_65_out, not_66_out, not_67_out, not_68_out, not_69_out, not_70_out, not_71_out,
       not_72_out, not_73_out, not_74_out, not_75_out, not_76_out, not_77_out, not_78_out, not_79_out,
       not_80_out, not_81_out, not_82_out, not_83_out, not_84_out, not_85_out, not_86_out, not_87_out,
       not_88_out, not_89_out, not_90_out, not_91_out, not_92_out, not_93_out, not_94_out, not_95_out,
       not_96_out, not_97_out, not_98_out, not_99_out, not_100_out, not_101_out, not_102_out, not_103_out,
       not_104_out, not_105_out, not_106_out, not_107_out, not_108_out, or_1_out, or_2_out, or_3_out,
       or_4_out, or_5_out, or_6_out, or_7_out, or_8_out, or_12_out, or_14_out;

  not not_1 (not_1_out, c);
  not not_2 (not_2_out, c);
  not not_3 (not_3_out, d);
  not not_4 (not_4_out, c);
  not not_5 (not_5_out, d);
  not not_6 (not_6_out, c);
  not not_7 (not_7_out, d);
  not not_8 (not_8_out, c);
  not not_9 (not_9_out, d);
  not not_10 (not_10_out, x2);
  not not_11 (not_11_out, x3);
  not not_12 (not_12_out, c);
  not not_13 (not_13_out, d);
  not not_14 (not_14_out, c);
  not not_15 (not_15_out, g);
  not not_16 (not_16_out, h);
  not not_17 (not_17_out, c);
  not not_18 (not_18_out, g);
  not not_19 (not_19_out, h);
  not not_20 (not_20_out, x2);
  not not_21 (not_21_out, x3);
  not not_22 (not_22_out, c);
  not not_23 (not_23_out, x2);
  not not_24 (not_24_out, x3);
  not not_25 (not_25_out, c);
  not not_26 (not_26_out, d);
  not not_27 (not_27_out, f);
  not not_28 (not_28_out, g);
  not not_29 (not_29_out, x2);
  and and_1 (and_1_out, not_1_out, d);
  not not_30 (not_30_out, e);
  not not_31 (not_31_out, f);
  not not_32 (not_32_out, g);
  not not_33 (not_33_out, h);
  not not_34 (not_34_out, x2);
  not not_35 (not_35_out, x4);
  and and_2 (and_2_out, not_2_out, not_3_out);
  not not_36 (not_36_out, e);
  not not_37 (not_37_out, f);
  not not_38 (not_38_out, x2);
  not not_39 (not_39_out, x4);
  and and_3 (and_3_out, not_4_out, not_5_out);
  not not_40 (not_40_out, e);
  not not_41 (not_41_out, g);
  not not_42 (not_42_out, h);
  not not_43 (not_43_out, x2);
  not not_44 (not_44_out, x4);
  and and_4 (and_4_out, not_6_out, not_7_out);
  not not_45 (not_45_out, e);
  not not_46 (not_46_out, g);
  not not_47 (not_47_out, x2);
  and and_5 (and_5_out, not_8_out, not_9_out);
  not not_48 (not_48_out, e);
  not not_49 (not_49_out, h);
  not not_50 (not_50_out, x2);
  and and_6 (and_6_out, not_10_out, not_11_out);
  not not_51 (not_51_out, x4);
  and and_7 (and_7_out, not_12_out, not_13_out);
  not not_52 (not_52_out, f);
  not not_53 (not_53_out, x2);
  not not_54 (not_54_out, x4);
  and and_8 (and_8_out, b, not_14_out);
  not not_55 (not_55_out, d);
  and and_9 (and_9_out, not_15_out, not_16_out);
  not not_56 (not_56_out, x2);
  not not_57 (not_57_out, x4);
  and and_10 (and_10_out, a, not_17_out);
  not not_58 (not_58_out, d);
  and and_11 (and_11_out, not_18_out, h);
  not not_59 (not_59_out, x2);
  not not_60 (not_60_out, x4);
  and and_12 (and_12_out, a, b);
  not not_61 (not_61_out, c);
  not not_62 (not_62_out, d);
  and and_13 (and_13_out, f, not_19_out);
  not not_63 (not_63_out, x2);
  not not_64 (not_64_out, x4);
  and and_14 (and_14_out, not_20_out, not_21_out);
  not not_65 (not_65_out, c);
  not not_66 (not_66_out, d);
  not not_67 (not_67_out, e);
  not not_68 (not_68_out, g);
  not not_69 (not_69_out, x2);
  not not_70 (not_70_out, x4);
  not not_71 (not_71_out, c);
  not not_72 (not_72_out, d);
  not not_73 (not_73_out, e);
  not not_74 (not_74_out, h);
  not not_75 (not_75_out, x2);
  not not_76 (not_76_out, x4);
  not not_77 (not_77_out, c);
  not not_78 (not_78_out, d);
  not not_79 (not_79_out, e);
  not not_80 (not_80_out, x2);
  not not_81 (not_81_out, x4);
  not not_82 (not_82_out, c);
  not not_83 (not_83_out, d);
  not not_84 (not_84_out, f);
  not not_85 (not_85_out, x2);
  and and_15 (and_15_out, b, not_22_out);
  not not_86 (not_86_out, d);
  not not_87 (not_87_out, g);
  not not_88 (not_88_out, h);
  not not_89 (not_89_out, x2);
  not not_90 (not_90_out, x4);
  not not_91 (not_91_out, c);
  not not_92 (not_92_out, d);
  not not_93 (not_93_out, g);
  not not_94 (not_94_out, x2);
  not not_95 (not_95_out, x4);
  and and_16 (and_16_out, not_23_out, not_24_out);
  not not_96 (not_96_out, x2);
  not not_97 (not_97_out, x3);
  and and_17 (and_17_out, not_25_out, not_26_out);
  and and_18 (and_18_out, e, not_27_out);
  and and_19 (and_19_out, not_28_out, not_29_out);
  not not_98 (not_98_out, c);
  not not_99 (not_99_out, d);
  not not_100 (not_100_out, f);
  not not_101 (not_101_out, h);
  not not_102 (not_102_out, x2);
  and and_20 (and_20_out, and_1_out, not_30_out);
  and and_21 (and_21_out, not_31_out, not_32_out);
  and and_22 (and_22_out, not_33_out, not_34_out);
  and and_23 (and_23_out, x3, not_35_out);
  and and_24 (and_24_out, and_2_out, not_36_out);
  and and_25 (and_25_out, not_37_out, g);
  and and_26 (and_26_out, h, not_38_out);
  and and_27 (and_27_out, x3, not_39_out);
  and and_28 (and_28_out, and_3_out, not_40_out);
  and and_29 (and_29_out, f, not_41_out);
  and and_30 (and_30_out, not_42_out, not_43_out);
  and and_31 (and_31_out, x3, not_44_out);
  and and_32 (and_32_out, and_4_out, not_45_out);
  and and_33 (and_33_out, f, not_46_out);
  and and_34 (and_34_out, h, not_47_out);
  and and_35 (and_35_out, x3, x4);
  and and_36 (and_36_out, and_5_out, not_48_out);
  and and_37 (and_37_out, f, g);
  and and_38 (and_38_out, not_49_out, not_50_out);
  and and_39 (and_39_out, x3, x4);
  and and_40 (z, and_6_out, not_51_out);
  and and_41 (and_41_out, and_7_out, e);
  and and_42 (and_42_out, not_52_out, g);
  and and_43 (and_43_out, h, not_53_out);
  and and_44 (and_44_out, x3, not_54_out);
  and and_45 (and_45_out, and_8_out, not_55_out);
  and and_46 (and_46_out, e, f);
  and and_47 (and_47_out, and_9_out, not_56_out);
  and and_48 (and_48_out, x3, not_57_out);
  and and_49 (and_49_out, and_10_out, not_58_out);
  and and_50 (and_50_out, e, f);
  and and_51 (and_51_out, and_11_out, not_59_out);
  and and_52 (and_52_out, x3, not_60_out);
  and and_53 (and_53_out, and_12_out, not_61_out);
  and and_54 (and_54_out, not_62_out, e);
  and and_55 (and_55_out, and_13_out, not_63_out);
  and and_56 (and_56_out, x3, not_64_out);
  and and_57 (v, and_14_out, x4);
  and and_58 (and_58_out, not_65_out, not_66_out);
  and and_59 (and_59_out, not_67_out, not_68_out);
  and and_60 (and_60_out, h, not_69_out);
  and and_61 (and_61_out, x3, not_70_out);
  and and_62 (and_62_out, not_71_out, not_72_out);
  and and_63 (and_63_out, not_73_out, g);
  and and_64 (and_64_out, not_74_out, not_75_out);
  and and_65 (and_65_out, x3, not_76_out);
  and and_66 (and_66_out, not_77_out, not_78_out);
  and and_67 (and_67_out, not_79_out, f);
  and and_68 (and_68_out, h, not_80_out);
  and and_69 (and_69_out, x3, not_81_out);
  and and_70 (and_70_out, not_82_out, not_83_out);
  and and_71 (and_71_out, e, not_84_out);
  and and_72 (and_72_out, not_85_out, x3);
  not not_103 (not_103_out, x4);
  and and_73 (and_73_out, and_15_out, not_86_out);
  and and_74 (and_74_out, e, not_87_out);
  and and_75 (and_75_out, not_88_out, not_89_out);
  and and_76 (and_76_out, x3, not_90_out);
  and and_77 (and_77_out, a, not_91_out);
  and and_78 (and_78_out, not_92_out, not_93_out);
  and and_79 (and_79_out, h, not_94_out);
  and and_80 (and_80_out, x3, not_95_out);
  and and_81 (and_81_out, a, b);
  not not_104 (not_104_out, c);
  not not_105 (not_105_out, d);
  not not_106 (not_106_out, h);
  not not_107 (not_107_out, x2);
  not not_108 (not_108_out, x4);
  and and_82 (s, and_16_out, x4);
  and and_83 (and_83_out, not_96_out, not_97_out);
  and and_84 (and_84_out, and_17_out, and_18_out);
  and and_85 (and_85_out, and_19_out, x4);
  and and_86 (and_86_out, not_98_out, not_99_out);
  and and_87 (and_87_out, e, not_100_out);
  and and_88 (and_88_out, not_101_out, not_102_out);
  and and_89 (and_89_out, and_20_out, and_21_out);
  and and_90 (and_90_out, and_22_out, and_23_out);
  and and_91 (and_91_out, and_24_out, and_25_out);
  and and_92 (and_92_out, and_26_out, and_27_out);
  and and_93 (and_93_out, and_28_out, and_29_out);
  and and_94 (and_94_out, and_30_out, and_31_out);
  and and_95 (and_95_out, and_32_out, and_33_out);
  and and_96 (and_96_out, and_34_out, and_35_out);
  and and_97 (and_97_out, and_36_out, and_37_out);
  and and_98 (and_98_out, and_38_out, and_39_out);
  and and_99 (and_99_out, and_41_out, and_42_out);
  and and_100 (and_100_out, and_43_out, and_44_out);
  and and_101 (and_101_out, and_45_out, and_46_out);
  and and_102 (and_102_out, and_47_out, and_48_out);
  and and_103 (and_103_out, and_49_out, and_50_out);
  and and_104 (and_104_out, and_51_out, and_52_out);
  and and_105 (and_105_out, and_53_out, and_54_out);
  and and_106 (and_106_out, and_55_out, and_56_out);
  and and_107 (and_107_out, and_58_out, and_59_out);
  and and_108 (and_108_out, and_60_out, and_61_out);
  and and_109 (and_109_out, and_62_out, and_63_out);
  and and_110 (and_110_out, and_64_out, and_65_out);
  and and_111 (and_111_out, and_66_out, and_67_out);
  and and_112 (and_112_out, and_68_out, and_69_out);
  and and_113 (and_113_out, and_70_out, and_71_out);
  and and_114 (and_114_out, and_72_out, not_103_out);
  and and_115 (and_115_out, and_73_out, and_74_out);
  and and_116 (and_116_out, and_75_out, and_76_out);
  and and_117 (and_117_out, and_77_out, and_78_out);
  and and_118 (and_118_out, and_79_out, and_80_out);
  and and_119 (and_119_out, and_81_out, not_104_out);
  and and_120 (and_120_out, not_105_out, e);
  and and_121 (and_121_out, not_106_out, not_107_out);
  and and_122 (and_122_out, x3, not_108_out);
  and and_123 (and_123_out, and_83_out, x4);
  and and_124 (and_124_out, and_84_out, and_85_out);
  and and_125 (and_125_out, and_86_out, and_87_out);
  and and_126 (and_126_out, and_88_out, x4);
  and and_127 (x, and_89_out, and_90_out);
  and and_128 (and_128_out, and_91_out, and_92_out);
  and and_129 (and_129_out, and_93_out, and_94_out);
  and and_130 (and_130_out, and_95_out, and_96_out);
  and and_131 (and_131_out, and_97_out, and_98_out);
  and and_132 (and_132_out, and_99_out, and_100_out);
  and and_133 (and_133_out, and_101_out, and_102_out);
  and and_134 (and_134_out, and_103_out, and_104_out);
  and and_135 (and_135_out, and_105_out, and_106_out);
  and and_136 (and_136_out, and_107_out, and_108_out);
  and and_137 (and_137_out, and_109_out, and_110_out);
  and and_138 (and_138_out, and_111_out, and_112_out);
  and and_139 (and_139_out, and_113_out, and_114_out);
  and and_140 (and_140_out, and_115_out, and_116_out);
  and and_141 (and_141_out, and_117_out, and_118_out);
  and and_142 (and_142_out, and_119_out, and_120_out);
  and and_143 (and_143_out, and_121_out, and_122_out);
  or or_1 (or_1_out, and_123_out, and_124_out);
  and and_144 (and_144_out, and_125_out, and_126_out);
  or or_2 (or_2_out, and_128_out, and_129_out);
  or or_3 (or_3_out, and_130_out, and_131_out);
  or or_4 (or_4_out, and_132_out, and_133_out);
  or or_5 (or_5_out, and_134_out, and_135_out);
  or or_6 (or_6_out, and_136_out, and_137_out);
  or or_7 (or_7_out, and_138_out, and_139_out);
  or or_8 (or_8_out, and_140_out, and_141_out);
  and and_145 (and_145_out, and_142_out, and_143_out);
  or or_9 (t, or_1_out, and_144_out);
  or or_10 (y, or_2_out, or_3_out);
  or or_11 (u, or_4_out, or_5_out);
  or or_12 (or_12_out, or_6_out, or_7_out);
  or or_13 (w, or_12_out, or_14_out);
  or or_14 (or_14_out, or_8_out, and_145_out);
endmodule
