// Logisim project Display.circ as structural Verilog: 1 circuit, main circuit main
module main (
  input  in_1,
  input  in_2,
  input  in_3,
  input  in_4,
  input  in_5,
  input  in_6,
  input  in_7,
  input  in_8,
  output [9:0] out_9,
  output [9:0] out_10
);

  wire bitselector_1_out, bitselector_2_out, bitselector_3_out, bitselector_4_out, bitselector_5_out,
       bitselector_6_out, bitselector_7_out, bitselector_8_out, clock_1_out, controlled_buffer_1_out,
       controlled_buffer_2_out, controlled_buffer_3_out, controlled_buffer_4_out, controlled_buffer_5_out,
       controlled_buffer_6_out, controlled_buffer_7_out, controlled_buffer_8_out, controlled_buffer_9_out,
       controlled_buffer_10_out, controlled_buffer_11_out, controlled_buffer_12_out,
       controlled_buffer_13_out, controlled_buffer_14_out, controlled_buffer_15_out,
       controlled_buffer_16_out, controlled_buffer_17_out, controlled_buffer_18_out,
       controlled_buffer_19_out, controlled_buffer_20_out, controlled_buffer_21_out,
       controlled_buffer_22_out, controlled_buffer_23_out, controlled_buffer_24_out,
       controlled_buffer_25_out, controlled_buffer_26_out, controlled_buffer_27_out,
       controlled_buffer_28_out, controlled_buffer_29_out, controlled_buffer_30_out,
       controlled_buffer_31_out, controlled_buffer_32_out, decoder_1_out0, decoder_1_out1, decoder_1_out2,
       decoder_1_out3;
  wire [1:0] counter_1_q;
  wire [7:0] adder_1_out, adder_2_out, adder_3_out, adder_4_out, adder_5_out, adder_6_out, adder_7_out,
       bit_extender_1_out, bit_extender_2_out, bit_extender_3_out, bit_extender_4_out, bit_extender_5_out,
       bit_extender_6_out, bit_extender_7_out, bit_extender_8_out, rom_1_data, shifter_1_out, shifter_2_out,
       shifter_3_out, shifter_4_out, shifter_5_out, shifter_6_out, shifter_7_out;
  wire [9:0] bit_extender_9_out, bit_extender_10_out;

  assign bit_extender_1_out = {{7{1'b0}}, in_3};  // Bit_Extender bit_extender_1
  assign bit_extender_2_out = {{7{1'b0}}, in_2};  // Bit_Extender bit_extender_2
  assign bit_extender_3_out = {{7{1'b0}}, in_1};  // Bit_Extender bit_extender_3
  assign bit_extender_4_out = {{7{1'b0}}, in_7};  // Bit_Extender bit_extender_4
  assign bit_extender_5_out = {{7{1'b0}}, in_6};  // Bit_Extender bit_extender_5
  assign bit_extender_6_out = {{7{1'b0}}, in_5};  // Bit_Extender bit_extender_6
  assign bit_extender_7_out = {{7{1'b0}}, in_4};  // Bit_Extender bit_extender_7
  Shifter shifter_1 (.in(bit_extender_7_out), .\dist (3'b100), .out(shifter_1_out));
  Shifter shifter_2 (.in(bit_extender_1_out), .\dist (3'b101), .out(shifter_2_out));
  Shifter shifter_3 (.in(bit_extender_2_out), .\dist (3'b110), .out(shifter_3_out));
  Shifter shifter_4 (.in(bit_extender_3_out), .\dist (3'b111), .out(shifter_4_out));
  assign bit_extender_8_out = {{7{1'b0}}, in_8};  // Bit_Extender bit_extender_8
  Shifter shifter_5 (.in(bit_extender_4_out), .\dist (3'b001), .out(shifter_5_out));
  Shifter shifter_6 (.in(bit_extender_5_out), .\dist (3'b010), .out(shifter_6_out));
  Shifter shifter_7 (.in(bit_extender_6_out), .\dist (3'b011), .out(shifter_7_out));
  Adder adder_1 (.a(shifter_2_out), .b(adder_2_out), .out(adder_1_out));  // open: cin, cout
  Adder adder_2 (.a(shifter_3_out), .b(shifter_4_out), .out(adder_2_out));  // open: cin, cout
  Adder adder_3 (.a(bit_extender_8_out), .b(shifter_5_out), .out(adder_3_out));  // open: cin, cout
  Adder adder_4 (.a(shifter_6_out), .b(shifter_7_out), .out(adder_4_out));  // open: cin, cout
  Adder adder_5 (.a(shifter_1_out), .b(adder_1_out), .out(adder_5_out));  // open: cin, cout
  Adder adder_6 (.a(adder_3_out), .b(adder_4_out), .out(adder_6_out));  // open: cin, cout
  Adder adder_7 (.a(adder_6_out), .b(adder_5_out), .out(adder_7_out));  // open: cin, cout
  assign bit_extender_9_out = {{8{1'b0}}, counter_1_q};  // Bit_Extender bit_extender_9
  Shifter #(.width(10)) shifter_8 (.in(bit_extender_9_out), .\dist (4'b1000), .out(out_10));
  assign bit_extender_10_out = {{2{1'b0}}, adder_7_out};  // Bit_Extender bit_extender_10
  Adder #(.width(10)) adder_8 (.a(bit_extender_10_out), .b(out_10), .out(out_9));  // open: cin, cout
  ROM #(.addrWidth(10)) rom_1 (.addr(out_9), .data(rom_1_data));  // open: sel
  BitSelector bitselector_1 (.in(rom_1_data), .out(bitselector_1_out), .sel(3'b001));
  BitSelector bitselector_2 (.in(rom_1_data), .out(bitselector_2_out), .sel(3'b010));
  BitSelector bitselector_3 (.in(rom_1_data), .out(bitselector_3_out), .sel(3'b111));
  BitSelector bitselector_4 (.in(rom_1_data), .out(bitselector_4_out), .sel(3'b110));
  BitSelector bitselector_5 (.in(rom_1_data), .out(bitselector_5_out), .sel(3'b000));
  BitSelector bitselector_6 (.in(rom_1_data), .out(bitselector_6_out), .sel(3'b101));
  BitSelector bitselector_7 (.in(rom_1_data), .out(bitselector_7_out), .sel(3'b100));
  BitSelector bitselector_8 (.in(rom_1_data), .out(bitselector_8_out), .sel(3'b011));
  assign controlled_buffer_1_out = decoder_1_out3 ? bitselector_1_out : 1'bz;  // Controlled_Buffer controlled_buffer_1
  assign controlled_buffer_2_out = decoder_1_out3 ? bitselector_3_out : 1'bz;  // Controlled_Buffer controlled_buffer_2
  assign controlled_buffer_3_out = decoder_1_out3 ? bitselector_4_out : 1'bz;  // Controlled_Buffer controlled_buffer_3
  assign controlled_buffer_4_out = decoder_1_out3 ? bitselector_2_out : 1'bz;  // Controlled_Buffer controlled_buffer_4
  _7_Segment_Display u_7_segment_display_1 (
    .g(controlled_buffer_1_out), .f(controlled_buffer_4_out), .a(controlled_buffer_2_out),
    .b(controlled_buffer_3_out), .e(controlled_buffer_5_out), .d(controlled_buffer_8_out),
    .c(controlled_buffer_7_out), .dp(controlled_buffer_6_out));
  assign controlled_buffer_5_out = decoder_1_out3 ? bitselector_8_out : 1'bz;  // Controlled_Buffer controlled_buffer_5
  assign controlled_buffer_6_out = decoder_1_out3 ? bitselector_5_out : 1'bz;  // Controlled_Buffer controlled_buffer_6
  assign controlled_buffer_7_out = decoder_1_out3 ? bitselector_6_out : 1'bz;  // Controlled_Buffer controlled_buffer_7
  assign controlled_buffer_8_out = decoder_1_out3 ? bitselector_7_out : 1'bz;  // Controlled_Buffer controlled_buffer_8
  assign controlled_buffer_9_out = decoder_1_out2 ? bitselector_3_out : 1'bz;  // Controlled_Buffer controlled_buffer_9
  assign controlled_buffer_10_out = decoder_1_out2 ? bitselector_1_out : 1'bz;  // Controlled_Buffer controlled_buffer_10
  assign controlled_buffer_11_out = decoder_1_out2 ? bitselector_4_out : 1'bz;  // Controlled_Buffer controlled_buffer_11
  assign controlled_buffer_12_out = decoder_1_out2 ? bitselector_2_out : 1'bz;  // Controlled_Buffer controlled_buffer_12
  _7_Segment_Display u_7_segment_display_2 (
    .g(controlled_buffer_10_out), .f(controlled_buffer_12_out), .a(controlled_buffer_9_out),
    .b(controlled_buffer_11_out), .e(controlled_buffer_16_out), .d(controlled_buffer_15_out),
    .c(controlled_buffer_14_out), .dp(controlled_buffer_13_out));
  assign controlled_buffer_13_out = decoder_1_out2 ? bitselector_5_out : 1'bz;  // Controlled_Buffer controlled_buffer_13
  assign controlled_buffer_14_out = decoder_1_out2 ? bitselector_6_out : 1'bz;  // Controlled_Buffer controlled_buffer_14
  assign controlled_buffer_15_out = decoder_1_out2 ? bitselector_7_out : 1'bz;  // Controlled_Buffer controlled_buffer_15
  assign controlled_buffer_16_out = decoder_1_out2 ? bitselector_8_out : 1'bz;  // Controlled_Buffer controlled_buffer_16
  assign controlled_buffer_17_out = decoder_1_out1 ? bitselector_3_out : 1'bz;  // Controlled_Buffer controlled_buffer_17
  assign controlled_buffer_18_out = decoder_1_out0 ? bitselector_2_out : 1'bz;  // Controlled_Buffer controlled_buffer_18
  assign controlled_buffer_19_out = decoder_1_out0 ? bitselector_1_out : 1'bz;  // Controlled_Buffer controlled_buffer_19
  assign controlled_buffer_20_out = decoder_1_out1 ? bitselector_1_out : 1'bz;  // Controlled_Buffer controlled_buffer_20
  assign controlled_buffer_21_out = decoder_1_out1 ? bitselector_2_out : 1'bz;  // Controlled_Buffer controlled_buffer_21
  assign controlled_buffer_22_out = decoder_1_out1 ? bitselector_4_out : 1'bz;  // Controlled_Buffer controlled_buffer_22
  _7_Segment_Display u_7_segment_display_3 (
    .g(controlled_buffer_20_out), .f(controlled_buffer_21_out), .a(controlled_buffer_17_out),
    .b(controlled_buffer_22_out), .e(controlled_buffer_26_out), .d(controlled_buffer_27_out),
    .c(controlled_buffer_24_out), .dp(controlled_buffer_23_out));
  _7_Segment_Display u_7_segment_display_4 (
    .g(controlled_buffer_19_out), .f(controlled_buffer_18_out), .a(controlled_buffer_29_out),
    .b(controlled_buffer_30_out), .e(controlled_buffer_25_out), .d(controlled_buffer_28_out),
    .c(controlled_buffer_32_out), .dp(controlled_buffer_31_out));
  assign controlled_buffer_23_out = decoder_1_out1 ? bitselector_5_out : 1'bz;  // Controlled_Buffer controlled_buffer_23
  assign controlled_buffer_24_out = decoder_1_out1 ? bitselector_6_out : 1'bz;  // Controlled_Buffer controlled_buffer_24
  assign controlled_buffer_25_out = decoder_1_out0 ? bitselector_8_out : 1'bz;  // Controlled_Buffer controlled_buffer_25
  assign controlled_buffer_26_out = decoder_1_out1 ? bitselector_8_out : 1'bz;  // Controlled_Buffer controlled_buffer_26
  assign controlled_buffer_27_out = decoder_1_out1 ? bitselector_7_out : 1'bz;  // Controlled_Buffer controlled_buffer_27
  assign controlled_buffer_28_out = decoder_1_out0 ? bitselector_7_out : 1'bz;  // Controlled_Buffer controlled_buffer_28
  assign controlled_buffer_29_out = decoder_1_out0 ? bitselector_3_out : 1'bz;  // Controlled_Buffer controlled_buffer_29
  assign controlled_buffer_30_out = decoder_1_out0 ? bitselector_4_out : 1'bz;  // Controlled_Buffer controlled_buffer_30
  assign controlled_buffer_31_out = decoder_1_out0 ? bitselector_5_out : 1'bz;  // Controlled_Buffer controlled_buffer_31
  assign controlled_buffer_32_out = decoder_1_out0 ? bitselector_6_out : 1'bz;  // Controlled_Buffer controlled_buffer_32
  Decoder #(.select(2), .enable("false")) decoder_1 (
    .out0(decoder_1_out0), .out1(decoder_1_out1), .out2(decoder_1_out2), .out3(decoder_1_out3),
    .sel(counter_1_q));
  Counter #(.width(2), .max('h3)) counter_1 (.Q(counter_1_q), .clk(clock_1_out));  // open: load, D, count, carry, clr
  Clock clock_1 (.out(clock_1_out));

  // Notes on the sheet:
  //   contents of rom_1 (hex, n*v repeats v):
  //   fc 60 da f2 66 b6 be e0 fe f6 fc 60 da f2 66 b6 be e0 fe f6 fc 60 da f2 66 b6 be e0 fe f6 fc 60 da
  //   f2 66 b6 be e0 fe f6 fc 60 da f2 66 b6 be e0 fe f6 fc 60 da f2 66 b6 be e0 fe f6 fc 60 da f2 66 b6
  //   be e0 fe f6 fc 60 da f2 66 b6 be e0 fe f6 fc 60 da f2 66 b6 be e0 fe f6 fc 60 da f2 66 b6 be e0 fe
  //   f6 fc 60 da f2 66 b6 be e0 fe f6 fc 60 da f2 66 b6 be e0 fe f6 fc 60 da f2 66 b6 be e0 fe f6 fc 60
  //   da f2 66 b6 be e0 fe f6 fc 60 da f2 66 b6 be e0 fe f6 fc 60 da f2 66 b6 be e0 fe f6 fc 60 da f2 66
  //   b6 be e0 fe f6 fc 60 da f2 66 b6 be e0 fe f6 fc 60 da f2 66 b6 be e0 fe f6 fc 60 da f2 66 b6 be e0
  //   fe f6 fc 60 da f2 66 b6 be e0 fe f6 fc 60 da f2 66 b6 be e0 fe f6 fc 60 da f2 66 b6 be e0 fe f6 fc
  //   60 da f2 66 b6 be e0 fe f6 fc 60 da f2 66 b6 be e0 fe f6 fc 60 da f2 66 b6 10*0 10*60 10*da 10*f2
  //   10*66 10*b6 10*be 10*e0 10*fe 10*f6 10*fc 10*60 10*da 10*f2 10*66 10*b6 10*be 10*e0 10*fe 10*f6
  //   10*fc 10*60 10*da 10*f2 10*66 6*b6 100*0 100*60 56*da
endmodule
