// Logisim project PC.circ as structural Verilog: 1 circuit, main circuit 8-bit PC
module _8_bit_PC (
  input  in_1,
  input  in_2,
  input  in_3,
  input  in_4,
  input  in_5,
  input  in_6,
  input  in_7,
  input  in_8,
  input  in_9,
  input  DIFF,
  input  in_11,
  input  A0,
  input  A1,
  input  B0,
  input  A2,
  input  B1,
  input  A3,
  input  B2,
  input  A4,
  input  B3,
  input  A5,
  input  B4,
  input  A6,
  input  B5,
  input  A7,
  input  B6,
  input  B7,
  input  in_28,
  input  in_29,
  input  Manual_Control,
  input  OUT_EN,
  input  CLEAR,
  input  LOAD,
  input  OUT_EN_2,
  input  OUT_EN_3,
  input  in_36,
  input  in_37,
  input  LOAD_2,
  input  LOAD_3,
  input  RO__not_RI,
  input  RE,
  input  CLEAR_2,
  input  in_43,
  input  in_44,
  input  in_45,
  input  in_46,
  input  in_47,
  input  in_48,
  input  in_49,
  input  in_50,
  input  in_51,
  input  in_52,
  input  in_53,
  input  in_54,
  input  in_55,
  input  in_56,
  input  in_57,
  input  in_58,
  output out_59,
  output out_60,
  output out_61,
  output out_62,
  output out_63,
  output out_64,
  output out_65,
  output out_66,
  output [9:0] out_67,
  output A_B_0,
  output A_B_1,
  output A_B_2,
  output A_B_3,
  output [9:0] out_72,
  output A_B_4,
  output A_B_5,
  output A_B_6,
  output A_B_7,
  output CARRY,
  output [1:0] out_78,
  output [1:0] out_79,
  output [10:0] out_80,
  output [7:0] out_81,
  output [7:0] out_82,
  output out_83,
  output out_84,
  output out_85,
  output out_86,
  output out_87,
  output out_88,
  output out_89,
  output out_90,
  output out_91,
  output out_92,
  output out_93,
  output out_94,
  output out_95,
  output out_96,
  output out_97,
  output out_98
);

  wire and_1_out, and_2_out, and_3_out, and_4_out, and_5_out, and_6_out, and_7_out, and_8_out, and_9_out,
       and_10_out, and_11_out, and_12_out, and_13_out, and_14_out, and_15_out, and_16_out, and_17_out,
       bitselector_35_out, bitselector_36_out, bitselector_37_out, bitselector_38_out, bitselector_39_out,
       bitselector_40_out, bitselector_41_out, bitselector_42_out, clock_1_out, clock_2_out, comparator_1_eq,
       comparator_2_gt, controlled_buffer_38_out, controlled_buffer_39_out, controlled_buffer_40_out,
       controlled_buffer_41_out, controlled_buffer_42_out, controlled_buffer_43_out,
       controlled_buffer_44_out, controlled_buffer_45_out, controlled_buffer_46_out,
       controlled_buffer_47_out, controlled_buffer_48_out, controlled_buffer_49_out,
       controlled_buffer_50_out, controlled_buffer_51_out, controlled_buffer_52_out,
       controlled_buffer_53_out, controlled_buffer_54_out, controlled_buffer_55_out,
       controlled_buffer_56_out, controlled_buffer_57_out, controlled_buffer_58_out,
       controlled_buffer_59_out, controlled_buffer_60_out, controlled_buffer_61_out,
       controlled_buffer_62_out, controlled_buffer_63_out, controlled_buffer_64_out,
       controlled_buffer_65_out, controlled_buffer_66_out, controlled_buffer_67_out,
       controlled_buffer_68_out, controlled_buffer_69_out, d_ff_9_q, d_ff_10_q, d_ff_11_q, d_ff_12_q,
       d_ff_13_q, d_ff_14_q, d_ff_15_q, d_ff_16_q, d_ff_17_q, d_ff_18_q, d_ff_19_q, d_ff_20_q, d_ff_21_q,
       d_ff_22_q, d_ff_23_q, d_ff_24_q, decoder_1_out0, decoder_1_out1, decoder_1_out2, decoder_1_out3,
       j_k_ff_1_q, j_k_ff_1_qn, nor_1_out, not_1_out, not_2_out, not_3_out, or_1_out, or_2_out, or_3_out,
       or_4_out, or_5_out, or_6_out, or_7_out, or_9_out, pull_resistor_22_node, pull_resistor_24_node,
       pull_resistor_25_node, xor_1_out, xor_2_out, xor_3_out, xor_4_out, xor_5_out, xor_6_out, xor_7_out,
       xor_8_out, xor_9_out, xor_10_out, xor_11_out, xor_12_out, xor_13_out, xor_14_out, xor_15_out,
       xor_16_out;
  wire [1:0] bit_extender_1_out, bit_extender_2_out, counter_3_q, shifter_1_out;
  wire [2:0] counter_2_q;
  wire [3:0] bit_extender_23_out, bit_extender_25_out, bit_extender_26_out;
  wire [7:0] adder_2_out, adder_3_out, adder_4_out, adder_5_out, adder_6_out, adder_7_out, adder_8_out,
       adder_9_out, adder_10_out, adder_11_out, adder_13_out, adder_14_out, adder_16_out, adder_17_out,
       bit_extender_4_out, bit_extender_5_out, bit_extender_7_out, bit_extender_8_out, bit_extender_9_out,
       bit_extender_10_out, bit_extender_11_out, bit_extender_12_out, bit_extender_13_out,
       bit_extender_14_out, bit_extender_15_out, bit_extender_16_out, bit_extender_17_out,
       bit_extender_18_out, bit_extender_19_out, bit_extender_20_out, controlled_buffer_25_out,
       controlled_buffer_33_out, controlled_buffer_34_out, controlled_buffer_35_out,
       controlled_buffer_37_out, controlled_buffer_75_out, controlled_buffer_77_out, counter_1_q,
       counter_4_q, divider_1_out, divider_2_rem, divider_3_out, divider_4_rem, divider_5_rem, or_10_out,
       ram_2_data, register_3_q, register_4_q, rom_1_data, rom_2_data, rom_3_data, rom_5_data, shifter_2_out,
       shifter_3_out, shifter_4_out, shifter_5_out, shifter_8_out, shifter_9_out, shifter_10_out,
       shifter_11_out, shifter_12_out, shifter_13_out, shifter_14_out, shifter_15_out, shifter_17_out,
       shifter_18_out;
  wire [9:0] bit_extender_22_out, bit_extender_24_out;
  wire [10:0] adder_12_out, bit_extender_3_out, bit_extender_6_out, bit_extender_21_out, shifter_6_out,
       shifter_7_out, shifter_16_out;

  Pull_Resistor pull_resistor_1 (.node(CLEAR));
  Clock clock_1 (.out(clock_1_out));
  and and_1 (and_1_out, ~in_36, clock_1_out, ~in_28);  // AND_Gate
  assign in_8 = OUT_EN_2 ? A0 : 1'bz;  // Controlled_Buffer controlled_buffer_1
  assign in_7 = OUT_EN_2 ? A1 : 1'bz;  // Controlled_Buffer controlled_buffer_2
  assign in_6 = OUT_EN_2 ? A2 : 1'bz;  // Controlled_Buffer controlled_buffer_3
  assign in_5 = OUT_EN_2 ? A3 : 1'bz;  // Controlled_Buffer controlled_buffer_4
  assign in_4 = OUT_EN_2 ? A4 : 1'bz;  // Controlled_Buffer controlled_buffer_5
  assign in_3 = OUT_EN_2 ? A5 : 1'bz;  // Controlled_Buffer controlled_buffer_6
  assign in_2 = OUT_EN_2 ? A6 : 1'bz;  // Controlled_Buffer controlled_buffer_7
  assign in_1 = OUT_EN_2 ? A7 : 1'bz;  // Controlled_Buffer controlled_buffer_8
  D_Flip_Flop d_ff_1 (.clk(and_1_out), .D(in_1), .Q(A7), .en(LOAD_2), .reset(CLEAR));  // open: Qn, preset
  D_Flip_Flop d_ff_2 (.clk(and_1_out), .D(in_2), .Q(A6), .en(LOAD_2), .reset(CLEAR));  // open: Qn, preset
  D_Flip_Flop d_ff_3 (.clk(and_1_out), .D(in_3), .Q(A5), .en(LOAD_2), .reset(CLEAR));  // open: Qn, preset
  D_Flip_Flop d_ff_4 (.clk(and_1_out), .D(in_4), .Q(A4), .en(LOAD_2), .reset(CLEAR));  // open: Qn, preset
  D_Flip_Flop d_ff_5 (.clk(and_1_out), .D(in_5), .Q(A3), .en(LOAD_2), .reset(CLEAR));  // open: Qn, preset
  D_Flip_Flop d_ff_6 (.clk(and_1_out), .D(in_6), .Q(A2), .en(LOAD_2), .reset(CLEAR));  // open: Qn, preset
  D_Flip_Flop d_ff_7 (.clk(and_1_out), .D(in_7), .Q(A1), .en(LOAD_2), .reset(CLEAR));  // open: Qn, preset
  D_Flip_Flop d_ff_8 (.clk(and_1_out), .D(in_8), .Q(A0), .en(LOAD_2), .reset(CLEAR));  // open: Qn, preset
  assign B7 = OUT_EN_3 ? d_ff_9_q : 1'bz;  // Controlled_Buffer controlled_buffer_9
  D_Flip_Flop d_ff_9 (.clk(and_1_out), .D(in_1), .Q(d_ff_9_q), .en(LOAD_3), .reset(CLEAR));  // open: Qn, preset
  D_Flip_Flop d_ff_10 (.clk(and_1_out), .D(in_2), .Q(d_ff_10_q), .en(LOAD_3), .reset(CLEAR));  // open: Qn, preset
  assign B6 = OUT_EN_3 ? d_ff_10_q : 1'bz;  // Controlled_Buffer controlled_buffer_10
  xor xor_1 (xor_1_out, DIFF, B0);
  xor xor_2 (xor_2_out, DIFF, B1);
  xor xor_3 (xor_3_out, DIFF, B2);
  xor xor_4 (xor_4_out, DIFF, B3);
  xor xor_5 (xor_5_out, DIFF, B4);
  xor xor_6 (xor_6_out, DIFF, B5);
  xor xor_7 (xor_7_out, DIFF, B6);
  xor xor_8 (xor_8_out, DIFF, B7);
  assign B5 = OUT_EN_3 ? d_ff_11_q : 1'bz;  // Controlled_Buffer controlled_buffer_11
  D_Flip_Flop d_ff_11 (.clk(and_1_out), .D(in_3), .Q(d_ff_11_q), .en(LOAD_3), .reset(CLEAR));  // open: Qn, preset
  assign B4 = OUT_EN_3 ? d_ff_12_q : 1'bz;  // Controlled_Buffer controlled_buffer_12
  D_Flip_Flop d_ff_12 (.clk(and_1_out), .D(in_4), .Q(d_ff_12_q), .en(LOAD_3), .reset(CLEAR));  // open: Qn, preset
  assign B3 = OUT_EN_3 ? d_ff_13_q : 1'bz;  // Controlled_Buffer controlled_buffer_13
  D_Flip_Flop d_ff_13 (.clk(and_1_out), .D(in_5), .Q(d_ff_13_q), .en(LOAD_3), .reset(CLEAR));  // open: Qn, preset
  assign B2 = OUT_EN_3 ? d_ff_14_q : 1'bz;  // Controlled_Buffer controlled_buffer_14
  D_Flip_Flop d_ff_14 (.clk(and_1_out), .D(in_6), .Q(d_ff_14_q), .en(LOAD_3), .reset(CLEAR));  // open: Qn, preset
  assign B1 = OUT_EN_3 ? d_ff_15_q : 1'bz;  // Controlled_Buffer controlled_buffer_15
  D_Flip_Flop d_ff_15 (.clk(and_1_out), .D(in_7), .Q(d_ff_15_q), .en(LOAD_3), .reset(CLEAR));  // open: Qn, preset
  assign B0 = OUT_EN_3 ? d_ff_16_q : 1'bz;  // Controlled_Buffer controlled_buffer_16
  D_Flip_Flop d_ff_16 (.clk(and_1_out), .D(in_8), .Q(d_ff_16_q), .en(LOAD_3), .reset(CLEAR));  // open: Qn, preset
  xor xor_9 (xor_9_out, A0, xor_1_out);
  xor xor_10 (xor_10_out, A1, xor_2_out);
  xor xor_11 (xor_11_out, A2, xor_3_out);
  xor xor_12 (xor_12_out, A3, xor_4_out);
  xor xor_13 (xor_13_out, A4, xor_5_out);
  xor xor_14 (xor_14_out, A5, xor_6_out);
  xor xor_15 (xor_15_out, A6, xor_7_out);
  xor xor_16 (xor_16_out, A7, xor_8_out);
  xor xor_17 (A_B_0, xor_9_out, DIFF);
  and and_2 (and_2_out, xor_9_out, DIFF);
  or or_1 (or_1_out, and_2_out, and_3_out);
  and and_3 (and_3_out, A0, xor_1_out);
  xor xor_18 (A_B_1, xor_10_out, or_1_out);
  and and_4 (and_4_out, xor_10_out, or_1_out);
  or or_2 (or_2_out, and_4_out, and_5_out);
  and and_5 (and_5_out, A1, xor_2_out);
  xor xor_19 (A_B_2, xor_11_out, or_2_out);
  and and_6 (and_6_out, xor_11_out, or_2_out);
  or or_3 (or_3_out, and_6_out, and_7_out);
  and and_7 (and_7_out, A2, xor_3_out);
  xor xor_20 (A_B_3, xor_12_out, or_3_out);
  and and_8 (and_8_out, xor_12_out, or_3_out);
  or or_4 (or_4_out, and_8_out, and_9_out);
  and and_9 (and_9_out, A3, xor_4_out);
  xor xor_21 (A_B_4, xor_13_out, or_4_out);
  and and_10 (and_10_out, xor_13_out, or_4_out);
  or or_5 (or_5_out, and_10_out, and_11_out);
  and and_11 (and_11_out, A4, xor_5_out);
  xor xor_22 (A_B_5, xor_14_out, or_5_out);
  and and_12 (and_12_out, xor_14_out, or_5_out);
  or or_6 (or_6_out, and_12_out, and_13_out);
  and and_13 (and_13_out, A5, xor_6_out);
  xor xor_23 (A_B_6, xor_15_out, or_6_out);
  and and_14 (and_14_out, xor_15_out, or_6_out);
  or or_7 (or_7_out, and_14_out, and_15_out);
  and and_15 (and_15_out, A6, xor_7_out);
  xor xor_24 (A_B_7, xor_16_out, or_7_out);
  and and_16 (and_16_out, xor_16_out, or_7_out);
  or or_8 (CARRY, and_16_out, and_17_out);
  and and_17 (and_17_out, A7, xor_8_out);
  nor nor_1 (nor_1_out, A_B_7, A_B_6, A_B_5, A_B_4, A_B_3, A_B_2, A_B_1, A_B_0);
  Adder #(.width(2)) adder_1 (.a(shifter_1_out), .b(bit_extender_1_out), .out(out_78));  // open: cin, cout
  assign bit_extender_1_out = {{1{1'b0}}, CARRY};  // Bit_Extender bit_extender_1
  assign in_8 = in_9 ? A_B_0 : 1'bz;  // Controlled_Buffer controlled_buffer_17
  assign in_7 = in_9 ? A_B_1 : 1'bz;  // Controlled_Buffer controlled_buffer_18
  assign in_6 = in_9 ? A_B_2 : 1'bz;  // Controlled_Buffer controlled_buffer_19
  assign in_5 = in_9 ? A_B_3 : 1'bz;  // Controlled_Buffer controlled_buffer_20
  assign in_4 = in_9 ? A_B_4 : 1'bz;  // Controlled_Buffer controlled_buffer_21
  assign in_3 = in_9 ? A_B_5 : 1'bz;  // Controlled_Buffer controlled_buffer_22
  assign in_2 = in_9 ? A_B_6 : 1'bz;  // Controlled_Buffer controlled_buffer_23
  assign in_1 = in_9 ? A_B_7 : 1'bz;  // Controlled_Buffer controlled_buffer_24
  Pull_Resistor pull_resistor_2 (.node(in_8));
  assign bit_extender_2_out = {{1{1'b0}}, nor_1_out};  // Bit_Extender bit_extender_2
  Shifter #(.width(2)) shifter_1 (.in(bit_extender_2_out), .\dist (1'b1), .out(shifter_1_out));
  Pull_Resistor pull_resistor_3 (.node(in_4));
  Pull_Resistor pull_resistor_4 (.node(in_7));
  Pull_Resistor pull_resistor_5 (.node(in_6));
  Pull_Resistor pull_resistor_6 (.node(in_5));
  Register #(.width(2)) register_1 (.D(out_78), .en(in_29), .Q(out_79), .clk(and_1_out));  // open: clr
  Pull_Resistor pull_resistor_7 (.node(in_2));
  Pull_Resistor pull_resistor_8 (.node(in_1));
  Pull_Resistor pull_resistor_9 (.node(in_3));
  BitSelector bitselector_1 (.in(controlled_buffer_77_out), .out(in_3), .sel(3'b101));
  BitSelector bitselector_2 (.in(controlled_buffer_77_out), .out(in_1), .sel(3'b111));
  BitSelector bitselector_3 (.in(controlled_buffer_77_out), .out(in_2), .sel(3'b110));
  BitSelector bitselector_4 (.in(controlled_buffer_77_out), .out(in_7), .sel(3'b001));
  BitSelector bitselector_5 (.in(controlled_buffer_77_out), .out(in_5), .sel(3'b011));
  BitSelector bitselector_6 (.in(controlled_buffer_77_out), .out(in_6), .sel(3'b010));
  BitSelector bitselector_7 (.in(controlled_buffer_77_out), .out(in_4), .sel(3'b100));
  BitSelector bitselector_8 (.in(controlled_buffer_77_out), .out(in_8), .sel(3'b000));
  BitSelector bitselector_9 (.in(controlled_buffer_25_out), .out(in_8), .sel(3'b000));
  BitSelector bitselector_10 (.in(controlled_buffer_25_out), .out(in_7), .sel(3'b001));
  BitSelector bitselector_11 (.in(controlled_buffer_25_out), .out(in_6), .sel(3'b010));
  BitSelector bitselector_12 (.in(controlled_buffer_25_out), .out(in_5), .sel(3'b011));
  BitSelector bitselector_13 (.in(controlled_buffer_25_out), .out(in_4), .sel(3'b100));
  BitSelector bitselector_14 (.in(controlled_buffer_25_out), .out(in_3), .sel(3'b101));
  BitSelector bitselector_15 (.in(controlled_buffer_25_out), .out(in_2), .sel(3'b110));
  BitSelector bitselector_16 (.in(controlled_buffer_25_out), .out(in_1), .sel(3'b111));
  assign bit_extender_3_out = {{9{1'b0}}, out_79};  // Bit_Extender bit_extender_3
  assign bit_extender_4_out = {{7{1'b0}}, in_1};  // Bit_Extender bit_extender_4
  assign bit_extender_5_out = {{7{1'b0}}, in_1};  // Bit_Extender bit_extender_5
  assign controlled_buffer_25_out = pull_resistor_22_node ? counter_1_q : 8'bz;  // Controlled_Buffer controlled_buffer_25
  assign bit_extender_6_out = {{3{1'b0}}, register_4_q};  // Bit_Extender bit_extender_6
  assign in_1 = OUT_EN ? d_ff_17_q : 1'bz;  // Controlled_Buffer controlled_buffer_26
  D_Flip_Flop d_ff_17 (.clk(and_1_out), .D(in_1), .Q(d_ff_17_q), .en(LOAD), .reset(CLEAR));  // open: Qn, preset
  assign bit_extender_7_out = {{7{1'b0}}, in_5};  // Bit_Extender bit_extender_7
  assign bit_extender_8_out = {{7{1'b0}}, in_4};  // Bit_Extender bit_extender_8
  assign bit_extender_9_out = {{7{1'b0}}, in_3};  // Bit_Extender bit_extender_9
  assign bit_extender_10_out = {{7{1'b0}}, in_2};  // Bit_Extender bit_extender_10
  Shifter shifter_2 (.in(bit_extender_10_out), .\dist (3'b110), .out(shifter_2_out));
  Shifter shifter_3 (.in(bit_extender_4_out), .\dist (3'b111), .out(shifter_3_out));
  assign bit_extender_11_out = {{7{1'b0}}, in_5};  // Bit_Extender bit_extender_11
  assign bit_extender_12_out = {{7{1'b0}}, in_4};  // Bit_Extender bit_extender_12
  assign bit_extender_13_out = {{7{1'b0}}, in_3};  // Bit_Extender bit_extender_13
  assign bit_extender_14_out = {{7{1'b0}}, in_2};  // Bit_Extender bit_extender_14
  Shifter shifter_4 (.in(bit_extender_14_out), .\dist (3'b110), .out(shifter_4_out));
  Shifter shifter_5 (.in(bit_extender_5_out), .\dist (3'b111), .out(shifter_5_out));
  Shifter #(.width(11)) shifter_6 (.in(bit_extender_3_out), .\dist (4'b1001), .out(shifter_6_out));
  Shifter #(.width(11)) shifter_7 (.in(bit_extender_6_out), .\dist (4'b0101), .out(shifter_7_out));
  not not_1 (not_1_out, and_1_out);
  assign in_2 = OUT_EN ? d_ff_18_q : 1'bz;  // Controlled_Buffer controlled_buffer_27
  D_Flip_Flop d_ff_18 (.clk(and_1_out), .D(in_2), .Q(d_ff_18_q), .en(LOAD), .reset(CLEAR));  // open: Qn, preset
  assign bit_extender_15_out = {{7{1'b0}}, in_8};  // Bit_Extender bit_extender_15
  assign bit_extender_16_out = {{7{1'b0}}, in_7};  // Bit_Extender bit_extender_16
  assign bit_extender_17_out = {{7{1'b0}}, in_6};  // Bit_Extender bit_extender_17
  Shifter shifter_8 (.in(bit_extender_17_out), .\dist (3'b010), .out(shifter_8_out));
  Shifter shifter_9 (.in(bit_extender_7_out), .\dist (3'b011), .out(shifter_9_out));
  Shifter shifter_10 (.in(bit_extender_8_out), .\dist (3'b100), .out(shifter_10_out));
  Shifter shifter_11 (.in(bit_extender_9_out), .\dist (3'b101), .out(shifter_11_out));
  Adder adder_2 (.a(shifter_2_out), .b(shifter_3_out), .out(adder_2_out));  // open: cin, cout
  assign bit_extender_18_out = {{7{1'b0}}, in_8};  // Bit_Extender bit_extender_18
  assign bit_extender_19_out = {{7{1'b0}}, in_7};  // Bit_Extender bit_extender_19
  assign bit_extender_20_out = {{7{1'b0}}, in_6};  // Bit_Extender bit_extender_20
  Shifter shifter_12 (.in(bit_extender_20_out), .\dist (3'b010), .out(shifter_12_out));
  Shifter shifter_13 (.in(bit_extender_11_out), .\dist (3'b011), .out(shifter_13_out));
  Shifter shifter_14 (.in(bit_extender_12_out), .\dist (3'b100), .out(shifter_14_out));
  Shifter shifter_15 (.in(bit_extender_13_out), .\dist (3'b101), .out(shifter_15_out));
  Adder adder_3 (.a(shifter_4_out), .b(shifter_5_out), .out(adder_3_out));  // open: cin, cout
  Counter counter_1 (
    .load(pull_resistor_24_node), .D(adder_17_out), .count(pull_resistor_25_node), .Q(counter_1_q),
    .clk(and_1_out), .clr(CLEAR));  // open: carry
  Shifter #(.width(11), .shift("lr")) shifter_16 (.in(shifter_7_out), .\dist (4'b0010), .out(shifter_16_out));
  assign bit_extender_21_out = {{8{1'b0}}, counter_2_q};  // Bit_Extender bit_extender_21
  Counter #(.width(3), .max('h7)) counter_2 (
    .Q(counter_2_q), .clk(not_1_out), .clr(or_9_out));  // open: load, D, count, carry
  or or_9 (or_9_out, comparator_1_eq, CLEAR);
  assign in_3 = OUT_EN ? d_ff_19_q : 1'bz;  // Controlled_Buffer controlled_buffer_28
  D_Flip_Flop d_ff_19 (.clk(and_1_out), .D(in_3), .Q(d_ff_19_q), .en(LOAD), .reset(CLEAR));  // open: Qn, preset
  Adder adder_4 (.a(bit_extender_15_out), .b(shifter_17_out), .out(adder_4_out));  // open: cin, cout
  Shifter shifter_17 (.in(bit_extender_16_out), .\dist (3'b001), .out(shifter_17_out));
  Adder adder_5 (.a(shifter_8_out), .b(shifter_9_out), .out(adder_5_out));  // open: cin, cout
  Adder adder_6 (.a(shifter_10_out), .b(adder_7_out), .out(adder_6_out));  // open: cin, cout
  Adder adder_7 (.a(shifter_11_out), .b(adder_2_out), .out(adder_7_out));  // open: cin, cout
  Adder adder_8 (.a(bit_extender_18_out), .b(shifter_18_out), .out(adder_8_out));  // open: cin, cout
  Shifter shifter_18 (.in(bit_extender_19_out), .\dist (3'b001), .out(shifter_18_out));
  Adder adder_9 (.a(shifter_12_out), .b(shifter_13_out), .out(adder_9_out));  // open: cin, cout
  Adder adder_10 (.a(shifter_14_out), .b(adder_11_out), .out(adder_10_out));  // open: cin, cout
  Adder adder_11 (.a(shifter_15_out), .b(adder_3_out), .out(adder_11_out));  // open: cin, cout
  Adder #(.width(11)) adder_12 (.a(shifter_6_out), .b(shifter_16_out), .out(adder_12_out));  // open: cin, cout
  assign in_4 = OUT_EN ? d_ff_20_q : 1'bz;  // Controlled_Buffer controlled_buffer_29
  D_Flip_Flop d_ff_20 (.clk(and_1_out), .D(in_4), .Q(d_ff_20_q), .en(LOAD), .reset(CLEAR));  // open: Qn, preset
  BitSelector bitselector_17 (.in(controlled_buffer_33_out), .out(in_1), .sel(3'b111));
  BitSelector bitselector_18 (.in(controlled_buffer_33_out), .out(in_2), .sel(3'b110));
  Adder adder_13 (.a(adder_4_out), .b(adder_5_out), .out(adder_13_out));  // open: cin, cout
  Adder adder_14 (.a(adder_8_out), .b(adder_9_out), .out(adder_14_out));  // open: cin, cout
  Adder #(.width(11)) adder_15 (.a(adder_12_out), .b(bit_extender_21_out), .out(out_80));  // open: cin, cout
  assign in_5 = OUT_EN ? d_ff_21_q : 1'bz;  // Controlled_Buffer controlled_buffer_30
  D_Flip_Flop d_ff_21 (.clk(and_1_out), .D(in_5), .Q(d_ff_21_q), .en(LOAD), .reset(CLEAR));  // open: Qn, preset
  BitSelector bitselector_19 (.in(controlled_buffer_33_out), .out(in_3), .sel(3'b101));
  BitSelector bitselector_20 (.in(controlled_buffer_33_out), .out(in_5), .sel(3'b011));
  BitSelector bitselector_21 (.in(controlled_buffer_33_out), .out(in_6), .sel(3'b010));
  BitSelector bitselector_22 (.in(controlled_buffer_33_out), .out(in_4), .sel(3'b100));
  Adder adder_16 (.a(adder_13_out), .b(adder_6_out), .out(adder_16_out));  // open: cin, cout
  Adder adder_17 (.a(adder_14_out), .b(adder_10_out), .out(adder_17_out));  // open: cin, cout
  D_Flip_Flop d_ff_22 (.clk(and_1_out), .D(in_6), .Q(d_ff_22_q), .en(LOAD), .reset(CLEAR));  // open: Qn, preset
  BitSelector bitselector_23 (.in(controlled_buffer_33_out), .out(in_7), .sel(3'b001));
  BitSelector bitselector_24 (.in(controlled_buffer_33_out), .out(in_8), .sel(3'b000));
  Register register_2 (.D(adder_16_out), .en(in_37), .Q(out_82), .clk(and_1_out), .clr(CLEAR));
  Divider divider_1 (.a(register_3_q), .b(8'h64), .out(divider_1_out));  // open: upper, rem
  Divider divider_2 (.a(divider_1_out), .b(8'ha), .rem(divider_2_rem));  // open: out, upper
  Divider divider_3 (.a(register_3_q), .b(8'ha), .out(divider_3_out));  // open: upper, rem
  Register register_3 (.D(adder_17_out), .en(in_11), .Q(register_3_q), .clk(and_1_out), .clr(CLEAR));
  Pull_Resistor pull_resistor_10 (.node(register_3_q));
  assign bit_extender_22_out = {{8{1'b0}}, counter_3_q};  // Bit_Extender bit_extender_22
  assign in_6 = OUT_EN ? d_ff_22_q : 1'bz;  // Controlled_Buffer controlled_buffer_31
  Hex_Digit_Display hex_digit_display_1 (.value(bit_extender_23_out));  // open: dp
  Bit_Extender #(.out_width(4)) bit_extender_23 (.in(divider_2_rem), .out(bit_extender_23_out));
  Divider divider_4 (.a(divider_3_out), .b(8'ha), .rem(divider_4_rem));  // open: out, upper
  Divider divider_5 (.a(register_3_q), .b(8'ha), .rem(divider_5_rem));  // open: out, upper
  assign bit_extender_24_out = {{2{1'b0}}, register_3_q};  // Bit_Extender bit_extender_24
  Shifter #(.width(10)) shifter_19 (.in(bit_extender_22_out), .\dist (4'b1000), .out(out_72));
  ROM #(.addrWidth(11)) rom_1 (.addr(out_80), .data(rom_1_data));  // open: sel
  ROM #(.addrWidth(11)) rom_2 (.addr(out_80), .data(rom_2_data));  // open: sel
  assign in_7 = OUT_EN ? d_ff_23_q : 1'bz;  // Controlled_Buffer controlled_buffer_32
  D_Flip_Flop d_ff_23 (.clk(and_1_out), .D(in_7), .Q(d_ff_23_q), .en(LOAD), .reset(CLEAR));  // open: Qn, preset
  assign controlled_buffer_33_out = RO__not_RI ? controlled_buffer_37_out : 8'bz;  // Controlled_Buffer controlled_buffer_33
  Hex_Digit_Display hex_digit_display_2 (.value(bit_extender_25_out));  // open: dp
  Bit_Extender #(.out_width(4)) bit_extender_25 (.in(divider_4_rem), .out(bit_extender_25_out));
  Bit_Extender #(.out_width(4)) bit_extender_26 (.in(divider_5_rem), .out(bit_extender_26_out));
  Adder #(.width(10)) adder_18 (.a(bit_extender_24_out), .b(out_72), .out(out_67));  // open: cin, cout
  Pull_Resistor pull_resistor_11 (.node(LOAD_2));
  Pull_Resistor pull_resistor_12 (.node(LOAD_3));
  Pull_Resistor pull_resistor_13 (.node(OUT_EN_2));
  BitSelector bitselector_25 (.in(controlled_buffer_34_out), .out(LOAD_3), .sel(3'b101));
  BitSelector bitselector_26 (.in(controlled_buffer_34_out), .out(LOAD_2), .sel(3'b111));
  BitSelector bitselector_27 (.in(controlled_buffer_34_out), .out(OUT_EN_2), .sel(3'b110));
  assign controlled_buffer_34_out = not_2_out ? rom_1_data : 8'bz;  // Controlled_Buffer controlled_buffer_34
  assign controlled_buffer_35_out = not_2_out ? rom_2_data : 8'bz;  // Controlled_Buffer controlled_buffer_35
  not not_2 (not_2_out, Manual_Control);
  assign or_10_out = rom_2_data | rom_1_data;  // OR_Gate or_10, 8 bits wide
  assign in_8 = OUT_EN ? d_ff_24_q : 1'bz;  // Controlled_Buffer controlled_buffer_36
  D_Flip_Flop d_ff_24 (.clk(and_1_out), .D(in_8), .Q(d_ff_24_q), .en(LOAD), .reset(CLEAR));  // open: Qn, preset
  not not_3 (not_3_out, RO__not_RI);
  assign controlled_buffer_37_out = not_3_out ? adder_16_out : 8'bz;  // Controlled_Buffer controlled_buffer_37
  RAM ram_1 (.addr(out_82), .data(controlled_buffer_37_out), .sel(RE), .clk(and_1_out), .ld(RO__not_RI));  // open: clr
  RAM ram_2 (.addr(out_82), .data(ram_2_data), .sel(RE), .clk(and_1_out), .ld(RO__not_RI));  // open: clr
  Hex_Digit_Display hex_digit_display_3 (.value(bit_extender_26_out));  // open: dp
  Pull_Resistor pull_resistor_14 (.node(in_11));
  Pull_Resistor pull_resistor_15 (.node(in_37));
  Pull_Resistor pull_resistor_16 (.node(DIFF));
  Pull_Resistor pull_resistor_17 (.node(in_9));
  BitSelector bitselector_28 (.in(controlled_buffer_34_out), .out(DIFF), .sel(3'b001));
  BitSelector bitselector_29 (.in(controlled_buffer_34_out), .out(in_11), .sel(3'b011));
  BitSelector bitselector_30 (.in(controlled_buffer_34_out), .out(in_37), .sel(3'b100));
  BitSelector bitselector_31 (.in(controlled_buffer_34_out), .out(in_9), .sel(3'b010));
  Comparator comparator_1 (.a(or_10_out), .b({8{1'b0}}), .eq(comparator_1_eq));  // open: gt, lt
  ROM #(.addrWidth(10)) rom_3 (.addr(out_67), .data(rom_3_data));  // open: sel
  Pull_Resistor pull_resistor_18 (.node(RE));
  Pull_Resistor pull_resistor_19 (.node(LOAD));
  Pull_Resistor pull_resistor_20 (.node(RO__not_RI));
  BitSelector bitselector_32 (.in(controlled_buffer_35_out), .out(RO__not_RI), .sel(3'b111));
  BitSelector bitselector_33 (.in(controlled_buffer_34_out), .out(RE), .sel(3'b000));
  BitSelector bitselector_34 (.in(controlled_buffer_35_out), .out(LOAD), .sel(3'b110));
  Pull_Resistor pull_resistor_21 (.node(controlled_buffer_37_out));
  BitSelector bitselector_35 (.in(rom_3_data), .out(bitselector_35_out), .sel(3'b001));
  BitSelector bitselector_36 (.in(rom_3_data), .out(bitselector_36_out), .sel(3'b010));
  BitSelector bitselector_37 (.in(rom_3_data), .out(bitselector_37_out), .sel(3'b111));
  BitSelector bitselector_38 (.in(rom_3_data), .out(bitselector_38_out), .sel(3'b110));
  BitSelector bitselector_39 (.in(rom_3_data), .out(bitselector_39_out), .sel(3'b000));
  BitSelector bitselector_40 (.in(rom_3_data), .out(bitselector_40_out), .sel(3'b101));
  BitSelector bitselector_41 (.in(rom_3_data), .out(bitselector_41_out), .sel(3'b100));
  BitSelector bitselector_42 (.in(rom_3_data), .out(bitselector_42_out), .sel(3'b011));
  Pull_Resistor pull_resistor_22 (.node(pull_resistor_22_node));
  Pull_Resistor pull_resistor_23 (.node(OUT_EN));
  Pull_Resistor pull_resistor_24 (.node(pull_resistor_24_node));
  Pull_Resistor pull_resistor_25 (.node(pull_resistor_25_node));
  BitSelector bitselector_43 (.in(controlled_buffer_35_out), .out(pull_resistor_24_node), .sel(3'b011));
  BitSelector bitselector_44 (.in(controlled_buffer_35_out), .out(OUT_EN), .sel(3'b101));
  BitSelector bitselector_45 (.in(controlled_buffer_35_out), .out(pull_resistor_25_node), .sel(3'b100));
  BitSelector bitselector_46 (.in(controlled_buffer_35_out), .out(pull_resistor_22_node), .sel(3'b010));
  Pull_Resistor pull_resistor_26 (.node(in_29));
  Pull_Resistor pull_resistor_27 (.node(in_28));
  BitSelector bitselector_47 (.in(controlled_buffer_35_out), .out(in_29), .sel(3'b001));
  BitSelector bitselector_48 (.in(controlled_buffer_35_out), .out(in_28), .sel(3'b000));
  Pull_Resistor pull_resistor_28 (.node(Manual_Control));
  assign controlled_buffer_38_out = decoder_1_out3 ? bitselector_35_out : 1'bz;  // Controlled_Buffer controlled_buffer_38
  _7_Segment_Display u_7_segment_display_1 (
    .g(controlled_buffer_38_out), .f(controlled_buffer_42_out), .a(controlled_buffer_40_out),
    .b(controlled_buffer_44_out), .e(controlled_buffer_39_out), .d(controlled_buffer_47_out),
    .c(controlled_buffer_49_out), .dp(controlled_buffer_46_out));
  assign controlled_buffer_39_out = decoder_1_out3 ? bitselector_42_out : 1'bz;  // Controlled_Buffer controlled_buffer_39
  Register register_4 (.D(ram_2_data), .en(LOAD), .Q(register_4_q), .clk(and_1_out), .clr(CLEAR));
  Pull_Resistor pull_resistor_29 (.node(ram_2_data));
  assign controlled_buffer_40_out = decoder_1_out3 ? bitselector_37_out : 1'bz;  // Controlled_Buffer controlled_buffer_40
  assign controlled_buffer_41_out = decoder_1_out2 ? bitselector_35_out : 1'bz;  // Controlled_Buffer controlled_buffer_41
  assign controlled_buffer_42_out = decoder_1_out3 ? bitselector_36_out : 1'bz;  // Controlled_Buffer controlled_buffer_42
  assign controlled_buffer_43_out = decoder_1_out2 ? bitselector_37_out : 1'bz;  // Controlled_Buffer controlled_buffer_43
  assign controlled_buffer_44_out = decoder_1_out3 ? bitselector_38_out : 1'bz;  // Controlled_Buffer controlled_buffer_44
  assign controlled_buffer_45_out = decoder_1_out2 ? bitselector_36_out : 1'bz;  // Controlled_Buffer controlled_buffer_45
  _7_Segment_Display u_7_segment_display_2 (
    .g(controlled_buffer_41_out), .f(controlled_buffer_45_out), .a(controlled_buffer_43_out),
    .b(controlled_buffer_53_out), .e(controlled_buffer_51_out), .d(controlled_buffer_48_out),
    .c(controlled_buffer_50_out), .dp(controlled_buffer_60_out));
  assign controlled_buffer_46_out = decoder_1_out3 ? bitselector_39_out : 1'bz;  // Controlled_Buffer controlled_buffer_46
  assign controlled_buffer_47_out = decoder_1_out3 ? bitselector_41_out : 1'bz;  // Controlled_Buffer controlled_buffer_47
  assign controlled_buffer_48_out = decoder_1_out2 ? bitselector_41_out : 1'bz;  // Controlled_Buffer controlled_buffer_48
  assign controlled_buffer_49_out = decoder_1_out3 ? bitselector_40_out : 1'bz;  // Controlled_Buffer controlled_buffer_49
  assign controlled_buffer_50_out = decoder_1_out2 ? bitselector_40_out : 1'bz;  // Controlled_Buffer controlled_buffer_50
  assign controlled_buffer_51_out = decoder_1_out2 ? bitselector_42_out : 1'bz;  // Controlled_Buffer controlled_buffer_51
  assign controlled_buffer_52_out = decoder_1_out1 ? bitselector_36_out : 1'bz;  // Controlled_Buffer controlled_buffer_52
  assign controlled_buffer_53_out = decoder_1_out2 ? bitselector_38_out : 1'bz;  // Controlled_Buffer controlled_buffer_53
  assign controlled_buffer_54_out = decoder_1_out1 ? bitselector_37_out : 1'bz;  // Controlled_Buffer controlled_buffer_54
  assign controlled_buffer_55_out = decoder_1_out1 ? bitselector_38_out : 1'bz;  // Controlled_Buffer controlled_buffer_55
  assign controlled_buffer_56_out = decoder_1_out1 ? bitselector_35_out : 1'bz;  // Controlled_Buffer controlled_buffer_56
  _7_Segment_Display u_7_segment_display_3 (
    .g(controlled_buffer_56_out), .f(controlled_buffer_52_out), .a(controlled_buffer_54_out),
    .b(controlled_buffer_55_out), .e(controlled_buffer_57_out), .d(controlled_buffer_59_out),
    .c(controlled_buffer_58_out), .dp(controlled_buffer_61_out));
  assign controlled_buffer_57_out = decoder_1_out1 ? bitselector_42_out : 1'bz;  // Controlled_Buffer controlled_buffer_57
  assign controlled_buffer_58_out = decoder_1_out1 ? bitselector_40_out : 1'bz;  // Controlled_Buffer controlled_buffer_58
  assign controlled_buffer_59_out = decoder_1_out1 ? bitselector_41_out : 1'bz;  // Controlled_Buffer controlled_buffer_59
  assign controlled_buffer_60_out = decoder_1_out2 ? bitselector_39_out : 1'bz;  // Controlled_Buffer controlled_buffer_60
  assign controlled_buffer_61_out = decoder_1_out1 ? bitselector_39_out : 1'bz;  // Controlled_Buffer controlled_buffer_61
  assign controlled_buffer_62_out = decoder_1_out0 ? bitselector_37_out : 1'bz;  // Controlled_Buffer controlled_buffer_62
  assign controlled_buffer_63_out = decoder_1_out0 ? bitselector_36_out : 1'bz;  // Controlled_Buffer controlled_buffer_63
  assign controlled_buffer_64_out = decoder_1_out0 ? bitselector_35_out : 1'bz;  // Controlled_Buffer controlled_buffer_64
  assign controlled_buffer_65_out = decoder_1_out0 ? bitselector_38_out : 1'bz;  // Controlled_Buffer controlled_buffer_65
  _7_Segment_Display u_7_segment_display_4 (
    .g(controlled_buffer_64_out), .f(controlled_buffer_63_out), .a(controlled_buffer_62_out),
    .b(controlled_buffer_65_out), .e(controlled_buffer_69_out), .d(controlled_buffer_67_out),
    .c(controlled_buffer_68_out), .dp(controlled_buffer_66_out));
  assign controlled_buffer_66_out = decoder_1_out0 ? bitselector_39_out : 1'bz;  // Controlled_Buffer controlled_buffer_66
  assign controlled_buffer_67_out = decoder_1_out0 ? bitselector_41_out : 1'bz;  // Controlled_Buffer controlled_buffer_67
  assign controlled_buffer_68_out = decoder_1_out0 ? bitselector_40_out : 1'bz;  // Controlled_Buffer controlled_buffer_68
  assign controlled_buffer_69_out = decoder_1_out0 ? bitselector_42_out : 1'bz;  // Controlled_Buffer controlled_buffer_69
  Counter #(.width(2), .max('h3)) counter_3 (.Q(counter_3_q), .clk(clock_2_out));  // open: load, D, count, carry, clr
  Clock clock_2 (.out(clock_2_out));
  Decoder #(.select(2), .enable("false")) decoder_1 (
    .out0(decoder_1_out0), .out1(decoder_1_out1), .out2(decoder_1_out2), .out3(decoder_1_out3),
    .sel(counter_3_q));
  Counter counter_4 (.count(comparator_2_gt), .Q(counter_4_q), .clk(j_k_ff_1_q), .clr(CLEAR));  // open: load, D, carry
  J_K_Flip_Flop j_k_ff_1 (
    .J(1'b1), .clk(and_1_out), .K(1'b1), .Q(j_k_ff_1_q), .Qn(j_k_ff_1_qn), .preset(CLEAR));  // open: en, reset
  assign in_37 = comparator_2_gt ? j_k_ff_1_q : 1'bz;  // Controlled_Buffer controlled_buffer_70
  assign RE = comparator_2_gt ? j_k_ff_1_qn : 1'bz;  // Controlled_Buffer controlled_buffer_71
  assign RO__not_RI = comparator_2_gt ? 1'b0 : 1'bz;  // Controlled_Buffer controlled_buffer_72
  Comparator comparator_2 (.a(out_81), .b({8{1'b1}}), .gt(comparator_2_gt));  // open: eq, lt
  assign Manual_Control = comparator_2_gt ? 1'b1 : 1'bz;  // Controlled_Buffer controlled_buffer_73
  assign ram_2_data = comparator_2_gt ? out_81 : 8'bz;  // Controlled_Buffer controlled_buffer_74
  assign controlled_buffer_75_out = j_k_ff_1_q ? counter_4_q : 8'bz;  // Controlled_Buffer controlled_buffer_75
  ROM rom_4 (.addr(counter_4_q), .data(out_81));  // open: sel
  ROM rom_5 (.addr(counter_4_q), .data(rom_5_data));  // open: sel
  assign controlled_buffer_75_out = j_k_ff_1_qn ? rom_5_data : 8'bz;  // Controlled_Buffer controlled_buffer_76
  assign controlled_buffer_77_out = comparator_2_gt ? controlled_buffer_75_out : 8'bz;  // Controlled_Buffer controlled_buffer_77

  assign CLEAR_2 = CLEAR;
  assign in_43 = in_1;
  assign in_44 = in_2;
  assign in_45 = in_3;
  assign in_46 = in_4;
  assign in_47 = in_5;
  assign in_48 = in_6;
  assign in_49 = in_7;
  assign in_50 = in_8;
  assign in_51 = in_1;
  assign in_52 = in_2;
  assign in_53 = in_3;
  assign in_54 = in_4;
  assign in_55 = in_5;
  assign in_56 = in_6;
  assign in_57 = in_7;
  assign in_58 = in_8;
  assign out_59 = in_1;
  assign out_60 = in_2;
  assign out_61 = in_3;
  assign out_62 = in_4;
  assign out_63 = in_5;
  assign out_64 = in_6;
  assign out_65 = in_7;
  assign out_66 = in_8;
  assign out_83 = A7;
  assign out_84 = A6;
  assign out_85 = A5;
  assign out_86 = A4;
  assign out_87 = A3;
  assign out_88 = A2;
  assign out_89 = A1;
  assign out_90 = A0;
  assign out_91 = B7;
  assign out_92 = B6;
  assign out_93 = B5;
  assign out_94 = B4;
  assign out_95 = B3;
  assign out_96 = B2;
  assign out_97 = B1;
  assign out_98 = B0;
  // also tied to VCC on the sheet: OUT_EN_3

  // Notes on the sheet:
  //   CLOCK
  //   A REGISTER
  //   ALU
  //   B REGISTER
  //   FLAGS
  //   MAIN BUS
  //   PROG COUNT
  //   LA  OA   LB  MI OUT  SO SDIFF   RE
  //   RO  IL  IO  CE  CL  CO  ///  HLT
  //   HIGH
  //   LOW
  //   INSTRUCTION REG (LOW BYTE, PARAM)
  //   contents of rom_1 (hex, n*v repeats v):
  //   10 1 6*0 10 1 80 5*0 10 1 20 5*0 10 1 84 5*0 10 1 86 5*0 10 1 20 84 4*0 10 1 20 86 4*0 10 1 10 41
  //   4*0 10 1 10 81 4*0 10 1 10 21 4*0 10 1 10 9 4*0 10 1 6*0 10 1 6*0 10 1 6*0 10 1 6*0 10 1 48 5*0 10 1
  //   6*0 10 1 6*0 10 1 6*0 10 1 6*0 10 1 6*0 10 1 6*0 10 1 6*0 10 1 6*0 10 1 6*0 10 1 6*0 10 1 6*0 10 1
  //   6*0 10 1 6*0 10 1 6*0 10 1 6*0 10 1 6*0 10 1 6*0 10 1 6*0 10 1 6*0 10 1 6*0 10 1 6*0 10 1 6*0 10 1
  //   6*0 10 1 6*0 10 1 6*0 10 1 6*0 10 1 6*0 10 1 6*0 10 1 6*0 10 1 6*0 10 1 6*0 10 1 6*0 10 1 6*0 10 1
  //   6*0 10 1 6*0 10 1 6*0 10 1 6*0 10 1 6*0 10 1 6*0 10 1 6*0 10 1 6*0 10 1 6*0 10 1 6*0 10 1 6*0 10 1
  //   6*0 10 1 6*0 10 1 6*0 10 1 6*0 10 1 6*0 10 1 80 5*0 10 1 20 5*0 10 1 84 5*0 10 1 86 5*0 10 1 20 84
  //   4*0 10 1 20 86 4*0 10 1 10 41 4*0 10 1 10 81 4*0 10 1 10 21 4*0 10 1 10 9 4*0 10 1 6*0 10 1 6*0 10 1
  //   6*0 10 1 6*0 10 1 48 5*0 10 1 6*0 10 1 6*0 10 1 6*0 10 1 6*0 10 1 6*0 10 1 6*0 10 1 6*0 10 1 6*0 10
  //   1 6*0 10 1 6*0 10 1 6*0 10 1 6*0 10 1 6*0 10 1 6*0 10 1 6*0 10 1 6*0 10 1 6*0 10 1 6*0 10 1 6*0 10 1
  //   6*0 10 1 6*0 10 1 6*0 10 1 6*0 10 1 6*0 10 1 6*0 10 1 6*0 10 1 6*0 10 1 6*0 10 1 6*0 10 1 6*0 10 1
  //   6*0 10 1 6*0 10 1 6*0 10 1 6*0 10 1 6*0 10 1 6*0 10 1 6*0 10 1 6*0 10 1 6*0 10 1 6*0 10 1 6*0 10 1
  //   6*0 10 1 6*0 10 1 6*0 10 1 6*0 10 1 6*0 10 1 6*0 10 1 6*0 10 1 6*0 10 1 80 5*0 10 1 20 5*0 10 1 84
  //   5*0 10 1 86 5*0 10 1 20 84 4*0 10 1 20 86 4*0 10 1 10 41 4*0 10 1 10 81 4*0 10 1 10 21 4*0 10 1 10 9
  //   4*0 10 1 6*0 10 1 6*0 10 1 6*0 10 1 6*0 10 1 48 5*0 10 1 6*0 10 1 6*0 10 1 6*0 10 1 6*0 10 1 6*0 10
  //   1 6*0 10 1 6*0 10 1 6*0 10 1 6*0 10 1 6*0 10 1 6*0 10 1 6*0 10 1 6*0 10 1 6*0 10 1 6*0 10 1 6*0 10 1
  //   6*0 10 1 6*0 10 1 6*0 10 1 6*0 10 1 6*0 10 1 6*0 10 1 6*0 10 1 6*0 10 1 6*0 10 1 6*0 10 1 6*0 10 1
  //   6*0 10 1 6*0 10 1 6*0 10 1 6*0 10 1 6*0 10 1 6*0 10 1 6*0 10 1 6*0 10 1 6*0 10 1 6*0 10 1 6*0 10 1
  //   6*0 10 1 6*0 10 1 6*0 10 1 6*0 10 1 6*0 10 1 6*0 10 1 6*0 10 1 6*0 10 1 6*0 10 1 6*0 10 1 6*0 10 1
  //   80 5*0 10 1 20 5*0 10 1 84 5*0 10 1 86 5*0 10 1 20 84 4*0 10 1 20 86 4*0 10 1 10 41 4*0 10 1 10 81
  //   4*0 10 1 10 21 4*0 10 1 10 9 4*0 10 1 6*0 10 1 6*0 10 1 6*0 10 1 6*0 10 1 48 5*0 10 1 6*0 10 1 6*0
  //   10 1 6*0 10 1 6*0 10 1 6*0 10 1 6*0 10 1 6*0 10 1 6*0 10 1 6*0 10 1 6*0 10 1 6*0 10 1 6*0 10 1 6*0
  //   10 1 6*0 10 1 6*0 10 1 6*0 10 1 6*0 10 1 6*0 10 1 6*0 10 1 6*0 10 1 6*0 10 1 6*0 10 1 6*0 10 1 6*0
  //   10 1 6*0 10 1 6*0 10 1 6*0 10 1 6*0 10 1 6*0 10 1 6*0 10 1 6*0 10 1 6*0 10 1 6*0 10 1 6*0 10 1 6*0
  //   10 1 6*0 10 1 6*0 10 1 6*0 10 1 6*0 10 1 6*0 10 1 6*0 10 1 6*0 10 1 6*0 10 1 6*0 10 1 6*0 10 1 6*0
  //   10 1 6*0 10 1
  //   contents of rom_2 (hex, n*v repeats v):
  //   4 d0 6*0 4 d0 20 5*0 4 d0 20 5*0 4 d0 2 5*0 4 d0 2 5*0 4 d0 20 2 4*0 4 d0 20 2 4*0 4 d0 20 5*0 4 d0
  //   20 80 4*0 4 d0 20 80 4*0 4 d0 20 80 4*0 4 d0 28 5*0 4 d0 6*0 4 d0 6*0 4 d0 6*0 4 d0 6*0 4 d0 1 5*0 4
  //   d0 6*0 4 d0 6*0 4 d0 6*0 4 d0 6*0 4 d0 6*0 4 d0 6*0 4 d0 6*0 4 d0 6*0 4 d0 6*0 4 d0 6*0 4 d0 6*0 4
  //   d0 6*0 4 d0 6*0 4 d0 6*0 4 d0 6*0 4 d0 6*0 4 d0 6*0 4 d0 6*0 4 d0 6*0 4 d0 6*0 4 d0 6*0 4 d0 6*0 4
  //   d0 6*0 4 d0 6*0 4 d0 6*0 4 d0 6*0 4 d0 6*0 4 d0 6*0 4 d0 6*0 4 d0 6*0 4 d0 6*0 4 d0 6*0 4 d0 6*0 4
  //   d0 6*0 4 d0 6*0 4 d0 6*0 4 d0 6*0 4 d0 6*0 4 d0 6*0 4 d0 6*0 4 d0 6*0 4 d0 6*0 4 d0 6*0 4 d0 6*0 4
  //   d0 6*0 4 d0 6*0 4 d0 6*0 4 d0 6*0 4 d0 20 5*0 4 d0 20 5*0 4 d0 2 5*0 4 d0 2 5*0 4 d0 20 2 4*0 4 d0
  //   20 2 4*0 4 d0 20 5*0 4 d0 20 80 4*0 4 d0 20 80 4*0 4 d0 20 80 4*0 4 d0 28 5*0 4 d0 28 5*0 4 d0 6*0 4
  //   d0 6*0 4 d0 6*0 4 d0 1 5*0 4 d0 6*0 4 d0 6*0 4 d0 6*0 4 d0 6*0 4 d0 6*0 4 d0 6*0 4 d0 6*0 4 d0 6*0 4
  //   d0 6*0 4 d0 6*0 4 d0 6*0 4 d0 6*0 4 d0 6*0 4 d0 6*0 4 d0 6*0 4 d0 6*0 4 d0 6*0 4 d0 6*0 4 d0 6*0 4
  //   d0 6*0 4 d0 6*0 4 d0 6*0 4 d0 6*0 4 d0 6*0 4 d0 6*0 4 d0 6*0 4 d0 6*0 4 d0 6*0 4 d0 6*0 4 d0 6*0 4
  //   d0 6*0 4 d0 6*0 4 d0 6*0 4 d0 6*0 4 d0 6*0 4 d0 6*0 4 d0 6*0 4 d0 6*0 4 d0 6*0 4 d0 6*0 4 d0 6*0 4
  //   d0 6*0 4 d0 6*0 4 d0 6*0 4 d0 6*0 4 d0 6*0 4 d0 6*0 4 d0 6*0 4 d0 20 5*0 4 d0 20 5*0 4 d0 2 5*0 4 d0
  //   2 5*0 4 d0 20 2 4*0 4 d0 20 2 4*0 4 d0 20 5*0 4 d0 20 80 4*0 4 d0 20 80 4*0 4 d0 20 80 4*0 4 d0 28
  //   5*0 4 d0 6*0 4 d0 28 5*0 4 d0 6*0 4 d0 6*0 4 d0 1 5*0 4 d0 6*0 4 d0 6*0 4 d0 6*0 4 d0 6*0 4 d0 6*0 4
  //   d0 6*0 4 d0 6*0 4 d0 6*0 4 d0 6*0 4 d0 6*0 4 d0 6*0 4 d0 6*0 4 d0 6*0 4 d0 6*0 4 d0 6*0 4 d0 6*0 4
  //   d0 6*0 4 d0 6*0 4 d0 6*0 4 d0 6*0 4 d0 6*0 4 d0 6*0 4 d0 6*0 4 d0 6*0 4 d0 6*0 4 d0 6*0 4 d0 6*0 4
  //   d0 6*0 4 d0 6*0 4 d0 6*0 4 d0 6*0 4 d0 6*0 4 d0 6*0 4 d0 6*0 4 d0 6*0 4 d0 6*0 4 d0 6*0 4 d0 6*0 4
  //   d0 6*0 4 d0 6*0 4 d0 6*0 4 d0 6*0 4 d0 6*0 4 d0 6*0 4 d0 6*0 4 d0 6*0 4 d0 6*0 4 d0 6*0 4 d0 20 5*0
  //   4 d0 20 5*0 4 d0 2 5*0 4 d0 2 5*0 4 d0 20 2 4*0 4 d0 20 2 4*0 4 d0 20 5*0 4 d0 20 80 4*0 4 d0 20 80
  //   4*0 4 d0 20 80 4*0 4 d0 28 5*0 4 d0 28 5*0 4 d0 28 5*0 4 d0 28 5*0 4 d0 6*0 4 d0 1 5*0 4 d0 6*0 4 d0
  //   6*0 4 d0 6*0 4 d0 6*0 4 d0 6*0 4 d0 6*0 4 d0 6*0 4 d0 6*0 4 d0 6*0 4 d0 6*0 4 d0 6*0 4 d0 6*0 4 d0
  //   6*0 4 d0 6*0 4 d0 6*0 4 d0 6*0 4 d0 6*0 4 d0 6*0 4 d0 6*0 4 d0 6*0 4 d0 6*0 4 d0 6*0 4 d0 6*0 4 d0
  //   6*0 4 d0 6*0 4 d0 6*0 4 d0 6*0 4 d0 6*0 4 d0 6*0 4 d0 6*0 4 d0 6*0 4 d0 6*0 4 d0 6*0 4 d0 6*0 4 d0
  //   6*0 4 d0 6*0 4 d0 6*0 4 d0 6*0 4 d0 6*0 4 d0 6*0 4 d0 6*0 4 d0 6*0 4 d0 6*0 4 d0 6*0 4 d0 6*0 4 d0
  //   6*0 4 d0
  //   Param
  //   Instrucrion
  //   DISPLAY DECODER
  //   CU
  //   IR LOW
  //   contents of rom_3 (hex, n*v repeats v):
  //   fc 60 da f2 66 b6 be e0 fe f6 fc 60 da f2 66 b6 be e0 fe f6 fc 60 da f2 66 b6 be e0 fe f6 fc 60 da
  //   f2 66 b6 be e0 fe f6 fc 60 da f2 66 b6 be e0 fe f6 fc 60 da f2 66 b6 be e0 fe f6 fc 60 da f2 66 b6
  //   be e0 fe f6 fc 60 da f2 66 b6 be e0 fe f6 fc 60 da f2 66 b6 be e0 fe f6 fc 60 da f2 66 b6 be e0 fe
  //   f6 fc 60 da f2 66 b6 be e0 fe f6 fc 60 da f2 66 b6 be e0 fe f6 fc 60 da f2 66 b6 be e0 fe f6 fc 60
  //   da f2 66 b6 be e0 fe f6 fc 60 da f2 66 b6 be e0 fe f6 fc 60 da f2 66 b6 be e0 fe f6 fc 60 da f2 66
  //   b6 be e0 fe f6 fc 60 da f2 66 b6 be e0 fe f6 fc 60 da f2 66 b6 be e0 fe f6 fc 60 da f2 66 b6 be e0
  //   fe f6 fc 60 da f2 66 b6 be e0 fe f6 fc 60 da f2 66 b6 be e0 fe f6 fc 60 da f2 66 b6 be e0 fe f6 fc
  //   60 da f2 66 b6 be e0 fe f6 fc 60 da f2 66 b6 be e0 fe f6 fc 60 da f2 66 b6 10*0 10*60 10*da 10*f2
  //   10*66 10*b6 10*be 10*e0 10*fe 10*f6 10*fc 10*60 10*da 10*f2 10*66 10*b6 10*be 10*e0 10*fe 10*f6
  //   10*fc 10*60 10*da 10*f2 10*66 6*b6 100*0 100*60 56*da
  //   RAM
  //   IR HIGH
  //   REG (HIGH BYTE)
  //   contents of rom_4 (hex, n*v repeats v):
  //   1 7 7 8 9 3 f 7 8 7 8 7 b ff
  //   contents of rom_5 (hex, n*v repeats v):
  //   1 32 33 32 33 0 0 34 32 33 34 32 3 ff
  //   BOOT LOADER
  //   HIGH
  //   LOW
endmodule
