// Logisim project RAM.circ as structural Verilog: 1 circuit, main circuit main
module main (
  input  in_1,
  input  in_2,
  input  in_3,
  input  in_4,
  input  in_5,
  input  in_6,
  input  in_7,
  input  in_8
);

  wire clock_1_out, undriven, undriven_2;
  wire [7:0] adder_1_out, adder_2_out, adder_3_out, adder_4_out, adder_5_out, adder_6_out, adder_7_out,
       bit_extender_1_out, bit_extender_2_out, bit_extender_3_out, bit_extender_4_out, bit_extender_5_out,
       bit_extender_6_out, bit_extender_7_out, bit_extender_8_out, ram_1_data, ram_2_data, shifter_1_out,
       shifter_2_out, shifter_3_out, shifter_4_out, shifter_5_out, shifter_6_out, shifter_7_out;

  assign bit_extender_1_out = {{7{1'b0}}, in_3};  // Bit_Extender bit_extender_1
  assign bit_extender_2_out = {{7{1'b0}}, in_2};  // Bit_Extender bit_extender_2
  assign bit_extender_3_out = {{7{1'b0}}, in_1};  // Bit_Extender bit_extender_3
  assign bit_extender_4_out = {{7{1'b0}}, in_7};  // Bit_Extender bit_extender_4
  assign bit_extender_5_out = {{7{1'b0}}, in_6};  // Bit_Extender bit_extender_5
  assign bit_extender_6_out = {{7{1'b0}}, in_5};  // Bit_Extender bit_extender_6
  assign bit_extender_7_out = {{7{1'b0}}, in_4};  // Bit_Extender bit_extender_7
  Shifter shifter_1 (.in(bit_extender_7_out), .\dist (3'b100), .out(shifter_1_out));
  Shifter shifter_2 (.in(bit_extender_1_out), .\dist (3'b101), .out(shifter_2_out));
  Shifter shifter_3 (.in(bit_extender_2_out), .\dist (3'b110), .out(shifter_3_out));
  Shifter shifter_4 (.in(bit_extender_3_out), .\dist (3'b111), .out(shifter_4_out));
  assign bit_extender_8_out = {{7{1'b0}}, in_8};  // Bit_Extender bit_extender_8
  Shifter shifter_5 (.in(bit_extender_4_out), .\dist (3'b001), .out(shifter_5_out));
  Shifter shifter_6 (.in(bit_extender_5_out), .\dist (3'b010), .out(shifter_6_out));
  Shifter shifter_7 (.in(bit_extender_6_out), .\dist (3'b011), .out(shifter_7_out));
  Adder adder_1 (.a(shifter_2_out), .b(adder_2_out), .out(adder_1_out));  // open: cin, cout
  Adder adder_2 (.a(shifter_3_out), .b(shifter_4_out), .out(adder_2_out));  // open: cin, cout
  Adder adder_3 (.a(bit_extender_8_out), .b(shifter_5_out), .out(adder_3_out));  // open: cin, cout
  Adder adder_4 (.a(shifter_6_out), .b(shifter_7_out), .out(adder_4_out));  // open: cin, cout
  Adder adder_5 (.a(shifter_1_out), .b(adder_1_out), .out(adder_5_out));  // open: cin, cout
  Adder adder_6 (.a(adder_3_out), .b(adder_4_out), .out(adder_6_out));  // open: cin, cout
  Adder adder_7 (.a(adder_6_out), .b(adder_5_out), .out(adder_7_out));  // open: cin, cout
  Clock clock_1 (.out(clock_1_out));
  RAM ram_1 (.addr(adder_7_out), .data(ram_1_data), .sel(undriven), .clk(clock_1_out), .ld(undriven_2));  // open: clr
  RAM ram_2 (.addr(adder_7_out), .data(ram_2_data), .sel(undriven), .clk(clock_1_out), .ld(undriven_2));  // open: clr

  // Notes on the sheet:
  //   Param
  //   Instrucrion
  //   RE
  //   RO  not(RI)
  //   IR LOW
  //   IR HIGH
endmodule
