// Logisim project Single_adder.circ as structural Verilog: 1 circuit, main circuit main
module main (
  input  A,
  input  B,
  input  CARRY,
  output S,
  output CARRY_2
);

  wire and_1_out, and_2_out, xor_1_out;

  xor xor_1 (xor_1_out, A, B);
  xor xor_2 (S, xor_1_out, CARRY);
  and and_1 (and_1_out, xor_1_out, CARRY);
  and and_2 (and_2_out, A, B);
  or or_1 (CARRY_2, and_1_out, and_2_out);
endmodule
