// Logisim project flip_flop.circ as structural Verilog: 1 circuit, main circuit main
module main (
  input  in_1,
  input  in_2,
  input  in_3
);

  wire and_1_out, and_2_out, clock_1_out, nor_1_out, nor_2_out;

  Clock clock_1 (.out(clock_1_out));
  and and_1 (and_1_out, nor_1_out, in_2, clock_1_out);
  and and_2 (and_2_out, clock_1_out, in_3, nor_2_out);
  nor nor_1 (nor_1_out, and_1_out, nor_2_out);
  nor nor_2 (nor_2_out, nor_1_out, and_2_out);
endmodule
