// Logisim project register.circ as structural Verilog: 1 circuit, main circuit main
module main (
  input  OUT_EN,
  input  LOAD,
  input  in_3,
  input  in_4,
  input  in_5,
  input  in_6,
  input  in_7,
  input  in_8,
  input  in_9,
  input  in_10,
  output out_11,
  output out_12,
  output out_13,
  output out_14,
  output out_15,
  output out_16,
  output out_17,
  output out_18
);

  wire clock_1_out, d_ff_1_q, d_ff_2_q, d_ff_3_q, d_ff_4_q, d_ff_5_q, d_ff_6_q, d_ff_7_q, d_ff_8_q;

  Clock clock_1 (.out(clock_1_out));
  assign out_11 = OUT_EN ? d_ff_1_q : 1'bz;  // Controlled_Buffer controlled_buffer_1
  D_Flip_Flop d_ff_1 (.clk(clock_1_out), .D(in_3), .Q(d_ff_1_q), .en(LOAD));  // open: Qn, preset, reset
  assign out_12 = OUT_EN ? d_ff_2_q : 1'bz;  // Controlled_Buffer controlled_buffer_2
  D_Flip_Flop d_ff_2 (.clk(clock_1_out), .D(in_4), .Q(d_ff_2_q), .en(LOAD));  // open: Qn, preset, reset
  assign out_13 = OUT_EN ? d_ff_3_q : 1'bz;  // Controlled_Buffer controlled_buffer_3
  D_Flip_Flop d_ff_3 (.clk(clock_1_out), .D(in_5), .Q(d_ff_3_q), .en(LOAD));  // open: Qn, preset, reset
  D_Flip_Flop d_ff_4 (.clk(clock_1_out), .D(in_6), .Q(d_ff_4_q), .en(LOAD));  // open: Qn, preset, reset
  assign out_14 = OUT_EN ? d_ff_4_q : 1'bz;  // Controlled_Buffer controlled_buffer_4
  assign out_15 = OUT_EN ? d_ff_5_q : 1'bz;  // Controlled_Buffer controlled_buffer_5
  D_Flip_Flop d_ff_5 (.clk(clock_1_out), .D(in_7), .Q(d_ff_5_q), .en(LOAD));  // open: Qn, preset, reset
  assign out_16 = OUT_EN ? d_ff_6_q : 1'bz;  // Controlled_Buffer controlled_buffer_6
  D_Flip_Flop d_ff_6 (.clk(clock_1_out), .D(in_8), .Q(d_ff_6_q), .en(LOAD));  // open: Qn, preset, reset
  assign out_17 = OUT_EN ? d_ff_7_q : 1'bz;  // Controlled_Buffer controlled_buffer_7
  D_Flip_Flop d_ff_7 (.clk(clock_1_out), .D(in_9), .Q(d_ff_7_q), .en(LOAD));  // open: Qn, preset, reset
  assign out_18 = OUT_EN ? d_ff_8_q : 1'bz;  // Controlled_Buffer controlled_buffer_8
  D_Flip_Flop d_ff_8 (.clk(clock_1_out), .D(in_10), .Q(d_ff_8_q), .en(LOAD));  // open: Qn, preset, reset
endmodule
